// Logisim project immediate_gen.circ as structural Verilog: 1 circuit, main circuit immediate_generator
module immediate_generator (
  input  [31:0] instruction,
  input  imm_gen_sel_i,
  output [31:0] imm_gen_o
);

  wire [31:0] bit_extender_1_out;

  assign bit_extender_1_out = {{20{instruction[31]}}, instruction[31:20]};  // Bit_Extender bit_extender_1
  // Probe on bit_extender_1_out
  // Probe on {instruction[31:12], {12{1'b0}}}
  Multiplexer #(.width(32)) multiplexer_1 (
    .in0(bit_extender_1_out), .in1({instruction[31:12], {12{1'b0}}}), .out(imm_gen_o), .sel(imm_gen_sel_i));

  // Notes on the sheet:
  //   I_TYPE
  //   U_TYPE
endmodule
